# Fritzing sketch camel-bulldog-gpio-led (saved by Fritzing 0.9.2b)

parts:
  Raspberry_Pi1 = Raspberry Pi 2
  LED1 = LEDs [package=led10mm]
  R1 = Resistor [tolerance=±5% resistance=1k package=THT]

nets:
  N1: Raspberry_Pi1.GPIO17, R1.Pin_0
  N2: Raspberry_Pi1.GND, LED1.A
  N3: LED1.C, R1.Pin_1
