# Fritzing sketch camel-bulldog-i2c-pca9685 (saved by Fritzing 0.9.2b)

parts:
  Součástka1 = 16-Channel 12-bit PCA9685 PWM/Servo Driver
  Raspberry_Pi1 = Raspberry Pi 2
  LED1 = LEDs [package=led10mm]

nets:
  N1: Součástka1.1, LED1.A
  GND: Součástka1.GND, Raspberry_Pi1.GND, LED1.C
  VCC: Součástka1.VCC, Raspberry_Pi1.5V
  N2: Součástka1.SDA, Raspberry_Pi1.GPIO2
  N3: Součástka1.SCL, Raspberry_Pi1.GPIO3

custom parts:
  16-Channel 12-bit PCA9685 PWM/Servo Driver: The Adafruit 16-Channel 12-bit PWM/Servo Driver will drive up to 16 servos over I2C with only 2 pins. The on-board PCA9685 PWM controller will drive all 16 channels simultaneously with no additional processing overhead. What's more, you can chain up to 62 of them to control up to 992 servos - all with the same 2 pins
